// Logisim project CU.circ as structural Verilog: 1 circuit, main circuit CtrlUnit
module CtrlUnit (
  input  [2:0] F3,
  input  S,
  input  Z,
  input  [6:0] F7,
  input  [6:0] opcode,
  output [1:0] ImmSrc,
  output [1:0] ResultSrc,
  output [1:0] PCSrc,
  output [2:0] ALUCtrl,
  output RegWrite,
  output ALUSrc,
  output MemWrite
);

  wire and_1_out, and_2_out, and_3_out, and_4_out, and_5_out, and_6_out, decoder_1_out0, decoder_1_out4,
       decoder_1_out12, decoder_1_out13, decoder_1_out27, decoder_2_out8, decoder_2_out9, decoder_2_out12,
       decoder_2_out13, decoder_2_out16, decoder_2_out17, decoder_2_out18, decoder_2_out20, decoder_2_out21,
       decoder_2_out22, decoder_2_out23, not_1_out, not_2_out, not_3_out;
  wire [4:3] decoder_1_out24;

  and and_1 (and_1_out, opcode[0], opcode[1]);
  not not_1 (not_1_out, S);
  not not_2 (not_2_out, Z);
  Decoder #(.select(5)) decoder_1 (
    .out0(decoder_1_out0), .out4(decoder_1_out4), .out8(MemWrite), .out12(decoder_1_out12),
    .out13(decoder_1_out13), .out24(decoder_1_out24[3]), .out25(PCSrc[1]), .out27(decoder_1_out27),
    .sel(opcode[6:2]), .en(and_1_out));  // open: out1, out2, out3, out5, out6, out7, out9, out10, out11, out14, out15, out16, out17, out18, out19, out20, out21, out22, out23, out26, out28, out29, out30, out31
  not not_3 (not_3_out, F3[0]);
  nor nor_1 (RegWrite, MemWrite, decoder_1_out24[3]);
  or or_1 (ImmSrc[1], decoder_1_out24[3], decoder_1_out27);
  or or_2 (ImmSrc[0], MemWrite, decoder_1_out27);
  nor nor_2 (ALUSrc, decoder_1_out12, decoder_1_out24[3]);
  or or_3 (ResultSrc[1], PCSrc[1], decoder_1_out27, decoder_1_out13);
  or or_4 (ResultSrc[0], decoder_1_out0, decoder_1_out13);
  and and_2 (and_2_out, Z, decoder_1_out24[3], not_3_out);
  or or_5 (PCSrc[0], decoder_1_out27, and_2_out, and_3_out, and_4_out, and_5_out);
  and and_3 (and_3_out, not_2_out, decoder_1_out24[3], F3[0]);
  and and_4 (and_4_out, S, decoder_1_out24[3], not_3_out);
  and and_5 (and_5_out, not_1_out, decoder_1_out24[3], F3[0]);
  or or_6 (decoder_1_out24[4], decoder_1_out12, decoder_1_out4);
  Decoder #(.select(5)) decoder_2 (
    .out8(decoder_2_out8), .out9(decoder_2_out9), .out12(decoder_2_out12), .out13(decoder_2_out13),
    .out16(decoder_2_out16), .out17(decoder_2_out17), .out18(decoder_2_out18), .out20(decoder_2_out20),
    .out21(decoder_2_out21), .out22(decoder_2_out22), .out23(decoder_2_out23), .sel({decoder_1_out24, F3}),
    .en(and_1_out));  // open: out0, out1, out2, out3, out4, out5, out6, out7, out10, out11, out14, out15, out19, out24, out25, out26, out27, out28, out29, out30, out31
  or or_7 (ALUCtrl[2], decoder_2_out18, decoder_2_out20, decoder_2_out17, decoder_2_out21);
  or or_8 (ALUCtrl[1], decoder_2_out22, decoder_2_out23, decoder_2_out17, decoder_2_out21);
  and and_6 (and_6_out, decoder_2_out16, F7[5], opcode[5]);
  or or_9 (ALUCtrl[0], decoder_2_out8, decoder_2_out9, decoder_2_out12, decoder_2_out13, and_6_out, decoder_2_out18, decoder_2_out22, decoder_2_out21);
endmodule
