// Logisim project ID.circ as structural Verilog: 1 circuit, main circuit InstrDec
module InstrDec (
  input  [31:0] Instr,
  output [6:0] op,
  output [24:0] Imm,
  output [4:0] A3,
  output [19:0] ImmU,
  output [2:0] f3,
  output [4:0] A1,
  output [4:0] A2,
  output [6:0] f7
);


  assign A1 = Instr[19:15];
  assign A2 = Instr[24:20];
  assign A3 = Instr[11:7];
  assign f3 = Instr[14:12];
  assign f7 = Instr[31:25];
  assign Imm = Instr[31:7];
  assign ImmU = Instr[31:12];
  assign op = Instr[6:0];
endmodule
