// Logisim project RF.circ as structural Verilog: 1 circuit, main circuit RegisterFile
module RegisterFile (
  input  WE,
  input  [4:0] Addr3,
  input  clk,
  input  [31:0] WD,
  input  [4:0] Addr2,
  input  [4:0] Addr1,
  output [31:0] RD1,
  output [31:0] RD2
);

  wire decoder_1_out1, decoder_1_out2, decoder_1_out3, decoder_1_out4, decoder_1_out5, decoder_1_out6,
       decoder_1_out7, decoder_1_out8, decoder_1_out9, decoder_1_out10, decoder_1_out11, decoder_1_out12,
       decoder_1_out13, decoder_1_out14, decoder_1_out15, decoder_1_out16, decoder_1_out17, decoder_1_out18,
       decoder_1_out19, decoder_1_out20, decoder_1_out21, decoder_1_out22, decoder_1_out23, decoder_1_out24,
       decoder_1_out25, decoder_1_out26, decoder_1_out27, decoder_1_out28, decoder_1_out29, decoder_1_out30,
       decoder_1_out31;
  wire [31:0] a0_q, a1_q, a2_q, a3_q, a4_q, a5_q, a6_q, a7_q, gp_q, ra_q, s0_q, s1_q, s2_q, s3_q, s4_q, s5_q,
       s6_q, s7_q, s8_q, s9_q, s10_q, s11_q, sp_q, t0_q, t1_q, t2_q, t3_q, t4_q, t5_q, t6_q, tp_q;

  Decoder #(.select(5)) decoder_1 (
    .out1(decoder_1_out1), .out2(decoder_1_out2), .out3(decoder_1_out3), .out4(decoder_1_out4),
    .out5(decoder_1_out5), .out6(decoder_1_out6), .out7(decoder_1_out7), .out8(decoder_1_out8),
    .out9(decoder_1_out9), .out10(decoder_1_out10), .out11(decoder_1_out11), .out12(decoder_1_out12),
    .out13(decoder_1_out13), .out14(decoder_1_out14), .out15(decoder_1_out15), .out16(decoder_1_out16),
    .out17(decoder_1_out17), .out18(decoder_1_out18), .out19(decoder_1_out19), .out20(decoder_1_out20),
    .out21(decoder_1_out21), .out22(decoder_1_out22), .out23(decoder_1_out23), .out24(decoder_1_out24),
    .out25(decoder_1_out25), .out26(decoder_1_out26), .out27(decoder_1_out27), .out28(decoder_1_out28),
    .out29(decoder_1_out29), .out30(decoder_1_out30), .out31(decoder_1_out31), .sel(Addr3), .en(WE));  // open: out0
  Register #(.width(32)) s0 (.D(WD), .en(decoder_1_out8), .clk(clk), .Q(s0_q));  // open: clr
  Register #(.width(32)) a6 (.D(WD), .en(decoder_1_out16), .clk(clk), .Q(a6_q));  // open: clr
  Register #(.width(32)) s8 (.D(WD), .en(decoder_1_out24), .clk(clk), .Q(s8_q));  // open: clr
  Register #(.width(32)) ra (.D(WD), .en(decoder_1_out1), .clk(clk), .Q(ra_q));  // open: clr
  Register #(.width(32)) s1 (.D(WD), .en(decoder_1_out9), .clk(clk), .Q(s1_q));  // open: clr
  Register #(.width(32)) a7 (.D(WD), .en(decoder_1_out17), .clk(clk), .Q(a7_q));  // open: clr
  Register #(.width(32)) s9 (.D(WD), .en(decoder_1_out25), .clk(clk), .Q(s9_q));  // open: clr
  Register #(.width(32)) sp (.D(WD), .en(decoder_1_out2), .clk(clk), .Q(sp_q));  // open: clr
  Register #(.width(32)) a0 (.D(WD), .en(decoder_1_out10), .clk(clk), .Q(a0_q));  // open: clr
  Register #(.width(32)) s2 (.D(WD), .en(decoder_1_out18), .clk(clk), .Q(s2_q));  // open: clr
  Register #(.width(32)) s10 (.D(WD), .en(decoder_1_out26), .clk(clk), .Q(s10_q));  // open: clr
  Register #(.width(32)) gp (.D(WD), .en(decoder_1_out3), .clk(clk), .Q(gp_q));  // open: clr
  Register #(.width(32)) a1 (.D(WD), .en(decoder_1_out11), .clk(clk), .Q(a1_q));  // open: clr
  Register #(.width(32)) s3 (.D(WD), .en(decoder_1_out19), .clk(clk), .Q(s3_q));  // open: clr
  Register #(.width(32)) s11 (.D(WD), .en(decoder_1_out27), .clk(clk), .Q(s11_q));  // open: clr
  Register #(.width(32)) tp (.D(WD), .en(decoder_1_out4), .clk(clk), .Q(tp_q));  // open: clr
  Register #(.width(32)) a2 (.D(WD), .en(decoder_1_out12), .clk(clk), .Q(a2_q));  // open: clr
  Register #(.width(32)) s4 (.D(WD), .en(decoder_1_out20), .clk(clk), .Q(s4_q));  // open: clr
  Register #(.width(32)) t3 (.D(WD), .en(decoder_1_out28), .clk(clk), .Q(t3_q));  // open: clr
  Register #(.width(32)) t0 (.D(WD), .en(decoder_1_out5), .clk(clk), .Q(t0_q));  // open: clr
  Register #(.width(32)) a3 (.D(WD), .en(decoder_1_out13), .clk(clk), .Q(a3_q));  // open: clr
  Register #(.width(32)) s5 (.D(WD), .en(decoder_1_out21), .clk(clk), .Q(s5_q));  // open: clr
  Register #(.width(32)) t4 (.D(WD), .en(decoder_1_out29), .clk(clk), .Q(t4_q));  // open: clr
  Register #(.width(32)) t1 (.D(WD), .en(decoder_1_out6), .clk(clk), .Q(t1_q));  // open: clr
  Register #(.width(32)) a4 (.D(WD), .en(decoder_1_out14), .clk(clk), .Q(a4_q));  // open: clr
  Register #(.width(32)) s6 (.D(WD), .en(decoder_1_out22), .clk(clk), .Q(s6_q));  // open: clr
  Register #(.width(32)) t5 (.D(WD), .en(decoder_1_out30), .clk(clk), .Q(t5_q));  // open: clr
  Register #(.width(32)) t2 (.D(WD), .en(decoder_1_out7), .clk(clk), .Q(t2_q));  // open: clr
  Register #(.width(32)) a5 (.D(WD), .en(decoder_1_out15), .clk(clk), .Q(a5_q));  // open: clr
  Register #(.width(32)) s7 (.D(WD), .en(decoder_1_out23), .clk(clk), .Q(s7_q));  // open: clr
  Register #(.width(32)) t6 (.D(WD), .en(decoder_1_out31), .clk(clk), .Q(t6_q));  // open: clr
  Multiplexer #(.enable("false"), .select(5), .width(32)) multiplexer_1 (
    .in0({32{1'b0}}), .in1(ra_q), .in2(sp_q), .in3(gp_q), .in4(tp_q), .in5(t0_q), .in6(t1_q), .in7(t2_q),
    .in8(s0_q), .in9(s1_q), .in10(a0_q), .in11(a1_q), .in12(a2_q), .in13(a3_q), .in14(a4_q), .in15(a5_q),
    .in16(a6_q), .in17(a7_q), .in18(s2_q), .in19(s3_q), .in20(s4_q), .in21(s5_q), .in22(s6_q), .in23(s7_q),
    .in24(s8_q), .in25(s9_q), .in26(s10_q), .in27(s11_q), .in28(t3_q), .in29(t4_q), .in30(t5_q), .in31(t6_q),
    .out(RD1), .sel(Addr1));
  Multiplexer #(.enable("false"), .select(5), .width(32)) multiplexer_2 (
    .in0({32{1'b0}}), .in1(ra_q), .in2(sp_q), .in3(gp_q), .in4(tp_q), .in5(t0_q), .in6(t1_q), .in7(t2_q),
    .in8(s0_q), .in9(s1_q), .in10(a0_q), .in11(a1_q), .in12(a2_q), .in13(a3_q), .in14(a4_q), .in15(a5_q),
    .in16(a6_q), .in17(a7_q), .in18(s2_q), .in19(s3_q), .in20(s4_q), .in21(s5_q), .in22(s6_q), .in23(s7_q),
    .in24(s8_q), .in25(s9_q), .in26(s10_q), .in27(s11_q), .in28(t3_q), .in29(t4_q), .in30(t5_q), .in31(t6_q),
    .out(RD2), .sel(Addr2));
endmodule
