// Logisim project SE.circ as structural Verilog: 1 circuit, main circuit main
module main (
  input  [24:0] Imm,
  input  [1:0] ImmSrc,
  output [31:0] Imm32
);

  wire [31:0] bit_extender_1_out, bit_extender_2_out, bit_extender_3_out, bit_extender_4_out;

  assign bit_extender_1_out = {{20{Imm[24]}}, Imm[24:13]};  // Bit_Extender bit_extender_1
  assign bit_extender_2_out = {{20{Imm[24]}}, {Imm[24:18], Imm[4:0]}};  // Bit_Extender bit_extender_2
  assign bit_extender_3_out = {{19{Imm[24]}}, {Imm[24], Imm[0], Imm[23:18], Imm[4:1], 1'b0}};  // Bit_Extender bit_extender_3
  assign bit_extender_4_out = {{11{Imm[24]}}, {Imm[24], Imm[12:5], Imm[13], Imm[23:14], 1'b0}};  // Bit_Extender bit_extender_4
  Multiplexer #(.enable("false"), .select(2), .width(32)) multiplexer_1 (
    .in0(bit_extender_1_out), .in1(bit_extender_2_out), .in2(bit_extender_3_out), .in3(bit_extender_4_out),
    .out(Imm32), .sel(ImmSrc));
endmodule
