// Logisim project Text.circ as structural Verilog: 1 circuit, main circuit Text
module Text (
  input  [31:0] A,
  output [31:0] Instr
);

  ROM #(.addrWidth(7), .dataWidth(32)) rom_1 (.addr(A[8:2]), .data(Instr));

  // Notes on the sheet:
  //   contents of rom_1 (hex, n*v repeats v):
  //   fd010113 2112823 2812623 3010413 1a000213 fc442e23 3400213 fe442023 d000213 fe442223 1a00213
  //   fe442423 d00213 fe442623 34000213 fe442823 600593 fdc40513 f4000ef fca42c23 fd842203 513 3012083
  //   2c12403 3010113 8067 fd010113 2112823 2812623 3010413 213 fe442623 213 fe442823 4058463 b55663
  //   fea42823 3c0006f fea42023 fcb42e23 fdc42583 fdc42203 fe042283 40428533 fb9ff0ef fea42623 feb42823
  //   fdc42583 fe042503 fec42203 120213 fe442623 fec42503 ff042583 3012083 2c12403 3010113 8067 fd010113
  //   2112823 2812623 3010413 2058863 feb42823 fea42023 fcb42e23 fdc42583 fe042503 f59ff0ef fcb42e23
  //   fdc42583 fe042503 ff042503 fd5ff06f 50513 3012083 2c12403 3010113 8067 fd010113 2112823 2812623
  //   3010413 52203 fe442823 100213 fe442623 fec42203 4b25263 feb42023 fca42e23 fec42203 221213 fdc42503
  //   450233 22583 ff042503 f65ff0ef fea42823 fe042583 fdc42503 fec42203 120213 fe442623 fbdff06f ff042503
  //   3012083 2c12403 3010113 8067
endmodule
