// Logisim project alu.circ as structural Verilog: 3 circuits, main circuit ALU_arch
module ALU_arch (
  input  [31:0] A,
  input  [31:0] B,
  input  [2:0] CTRL,
  output ZF,
  output SF,
  output [31:0] F
);

  wire [31:0] adder_1_out, and_1_out, multiplexer_1_out, not_1_out, or_1_out, shifter_1_out, shifter_2_out,
       SLT_f, xor_1_out;

  assign not_1_out = ~B;  // NOT_Gate not_1, 32 bits wide
  Multiplexer #(.enable("false"), .width(32)) multiplexer_1 (
    .in0(B), .in1(not_1_out), .out(multiplexer_1_out), .sel(CTRL[0]));
  Adder #(.width(32)) adder_1 (.a(A), .b(multiplexer_1_out), .out(adder_1_out), .cin(CTRL[0]));  // open: cout
  assign and_1_out = A & B;  // AND_Gate and_1, 32 bits wide
  assign or_1_out = A | B;  // OR_Gate or_1, 32 bits wide
  assign xor_1_out = A ^ B;  // XOR_Gate xor_1, 32 bits wide
  S SLT (.I32(adder_1_out), .SF(SF), .F(SLT_f));
  Shifter #(.width(32)) shifter_1 (.in(A), .\dist (B[4:0]), .out(shifter_1_out));
  Shifter #(.shift("lr"), .width(32)) shifter_2 (.in(A), .\dist (B[4:0]), .out(shifter_2_out));
  Z NORGate (.I32(adder_1_out), .ZF(ZF));
  Multiplexer #(.enable("false"), .select(3), .width(32)) multiplexer_2 (
    .in0(adder_1_out), .in1(adder_1_out), .in2(and_1_out), .in3(or_1_out), .in4(xor_1_out), .in5(SLT_f),
    .in6(shifter_1_out), .in7(shifter_2_out), .out(F), .sel(CTRL));
endmodule

module Z (
  input  [31:0] I32,
  output ZF
);

  nor nor_1 (ZF, I32[0], I32[1], I32[2], I32[3], I32[4], I32[5], I32[6], I32[7], I32[8], I32[9], I32[10], I32[11], I32[12], I32[13], I32[14], I32[15], I32[17], I32[18], I32[19], I32[20], I32[21], I32[22], I32[23], I32[24], I32[25], I32[26], I32[27], I32[28], I32[29], I32[30], I32[31], I32[16]);
endmodule

module S (
  input  [31:0] I32,
  output SF,
  output [31:0] F
);


  assign F = {{31{1'b0}}, I32[31]};
  assign SF = I32[31];
endmodule
