// Logisim project riscv.circ as structural Verilog: 10 circuits, main circuit Processor
module Processor (
  input  clk,
  input  clr,
  output [31:0] rs1,
  output [31:0] rs2,
  output [31:0] Instruction,
  output [31:0] ALUOUT
);

  wire alu_1_sf, alu_1_zf, ctrlunit_1_alusrc, ctrlunit_1_memwrite, ctrlunit_1_regwrite, not_1_out;
  wire [1:0] ctrlunit_1_immsrc, ctrlunit_1_pcsrc, ctrlunit_1_resultsrc;
  wire [2:0] ctrlunit_1_aluctrl, instrdec_1_f3;
  wire [4:0] instrdec_1_a1, instrdec_1_a2, instrdec_1_a3;
  wire [6:0] instrdec_1_f7, instrdec_1_op;
  wire [19:0] instrdec_1_immu;
  wire [24:0] instrdec_1_imm;
  wire [31:0] adder_1_out, adder_2_out, Data_dout, multiplexer_1_out, multiplexer_2_out, multiplexer_3_out,
       PC_q, signext_1_imm32, sll12_1_uimm32;

  Multiplexer #(.enable("false"), .select(2), .width(32)) multiplexer_1 (
    .in0(adder_1_out), .in1(adder_2_out), .in2(ALUOUT), .in3(ALUOUT), .out(multiplexer_1_out),
    .sel(ctrlunit_1_pcsrc));
  Register #(.width(32)) PC (.D(multiplexer_1_out), .en(1'b1), .clk(clk), .Q(PC_q), .clr(clr));
  GGCD ggcd_1 (.Instr(Instruction), .A(PC_q));
  Adder #(.width(32)) adder_1 (.a(PC_q), .b(32'h4), .out(adder_1_out), .cin(1'b0));  // open: cout
  Adder #(.width(32)) adder_2 (.a(PC_q), .b(signext_1_imm32), .out(adder_2_out), .cin(1'b0));  // open: cout
  InstrDec instrdec_1 (
    .op(instrdec_1_op), .Imm(instrdec_1_imm), .A3(instrdec_1_a3), .ImmU(instrdec_1_immu), .f3(instrdec_1_f3),
    .A1(instrdec_1_a1), .A2(instrdec_1_a2), .f7(instrdec_1_f7), .Instr(Instruction));
  RegFile regfile_1 (
    .RD1(rs1), .RD2(rs2), .clk(clk), .WE(ctrlunit_1_regwrite), .Addr2(instrdec_1_a2), .Addr1(instrdec_1_a1),
    .Addr3(instrdec_1_a3), .WD(multiplexer_3_out));
  SignExt signext_1 (.Imm32(signext_1_imm32), .Imm(instrdec_1_imm), .ImmSrc(ctrlunit_1_immsrc));
  sll12 sll12_1 (.UImm32(sll12_1_uimm32), .UImm(instrdec_1_immu));
  not not_1 (not_1_out, ctrlunit_1_memwrite);
  CtrlUnit ctrlunit_1 (
    .ALUSrc(ctrlunit_1_alusrc), .MemWrite(ctrlunit_1_memwrite), .ResultSrc(ctrlunit_1_resultsrc),
    .PCSrc(ctrlunit_1_pcsrc), .ALUCtrl(ctrlunit_1_aluctrl), .RegWrite(ctrlunit_1_regwrite),
    .ImmSrc(ctrlunit_1_immsrc), .F7(instrdec_1_f7), .opcode(instrdec_1_op), .S(alu_1_sf), .Z(alu_1_zf),
    .F3(instrdec_1_f3));
  RAM #(.addrWidth(11), .asyncread("true"), .dataWidth(32)) Data (
    .addr(ALUOUT[12:2]), .we(ctrlunit_1_memwrite), .oe(not_1_out), .clk(clk), .din(rs2), .dout(Data_dout));
  Multiplexer #(.enable("false"), .width(32)) multiplexer_2 (
    .in0(rs2), .in1(signext_1_imm32), .out(multiplexer_2_out), .sel(ctrlunit_1_alusrc));
  ALU alu_1 (.F(ALUOUT), .ZF(alu_1_zf), .SF(alu_1_sf), .A(rs1), .B(multiplexer_2_out), .CTRL(ctrlunit_1_aluctrl));
  Multiplexer #(.enable("false"), .select(2), .width(32)) multiplexer_3 (
    .in0(ALUOUT), .in1(Data_dout), .in2(adder_1_out), .in3(sll12_1_uimm32), .out(multiplexer_3_out),
    .sel(ctrlunit_1_resultsrc));
endmodule

module ALU (
  input  [31:0] A,
  input  [31:0] B,
  input  [2:0] CTRL,
  output ZF,
  output SF,
  output [31:0] F
);

  wire [31:0] adder_1_out, and_1_out, multiplexer_1_out, not_1_out, or_1_out, shifter_1_out, shifter_2_out,
       SLT_f, xor_1_out;

  assign not_1_out = ~B;  // NOT_Gate not_1, 32 bits wide
  Multiplexer #(.enable("false"), .width(32)) multiplexer_1 (
    .in0(B), .in1(not_1_out), .out(multiplexer_1_out), .sel(CTRL[0]));
  Adder #(.width(32)) adder_1 (.a(A), .b(multiplexer_1_out), .out(adder_1_out), .cin(CTRL[0]));  // open: cout
  assign and_1_out = A & B;  // AND_Gate and_1, 32 bits wide
  assign or_1_out = A | B;  // OR_Gate or_1, 32 bits wide
  assign xor_1_out = A ^ B;  // XOR_Gate xor_1, 32 bits wide
  S SLT (.I32(adder_1_out), .SF(SF), .F(SLT_f));
  Shifter #(.width(32)) shifter_1 (.in(A), .\dist (B[4:0]), .out(shifter_1_out));
  Shifter #(.shift("lr"), .width(32)) shifter_2 (.in(A), .\dist (B[4:0]), .out(shifter_2_out));
  Z NORGate (.I32(adder_1_out), .ZF(ZF));
  Multiplexer #(.enable("false"), .select(3), .width(32)) multiplexer_2 (
    .in0(adder_1_out), .in1(adder_1_out), .in2(and_1_out), .in3(or_1_out), .in4(xor_1_out), .in5(SLT_f),
    .in6(shifter_1_out), .in7(shifter_2_out), .out(F), .sel(CTRL));
endmodule

module CtrlUnit (
  input  [2:0] F3,
  input  S,
  input  Z,
  input  [6:0] F7,
  input  [6:0] opcode,
  output [1:0] ImmSrc,
  output [1:0] ResultSrc,
  output [1:0] PCSrc,
  output [2:0] ALUCtrl,
  output RegWrite,
  output ALUSrc,
  output MemWrite
);

  wire and_1_out, and_2_out, and_3_out, and_4_out, and_5_out, and_6_out, decoder_1_out0, decoder_1_out4,
       decoder_1_out12, decoder_1_out13, decoder_1_out27, decoder_2_out8, decoder_2_out9, decoder_2_out12,
       decoder_2_out13, decoder_2_out16, decoder_2_out17, decoder_2_out18, decoder_2_out20, decoder_2_out21,
       decoder_2_out22, decoder_2_out23, not_1_out, not_2_out, not_3_out, not_4_out;
  wire [4:3] decoder_1_out24;

  and and_1 (and_1_out, opcode[0], opcode[1]);
  not not_1 (not_1_out, S);
  not not_2 (not_2_out, Z);
  Decoder #(.select(5)) decoder_1 (
    .out0(decoder_1_out0), .out4(decoder_1_out4), .out8(MemWrite), .out12(decoder_1_out12),
    .out13(decoder_1_out13), .out24(decoder_1_out24[3]), .out25(PCSrc[1]), .out27(decoder_1_out27),
    .sel(opcode[6:2]), .en(and_1_out));  // open: out1, out2, out3, out5, out6, out7, out9, out10, out11, out14, out15, out16, out17, out18, out19, out20, out21, out22, out23, out26, out28, out29, out30, out31
  not not_3 (not_3_out, F3[0]);
  not not_4 (not_4_out, F3[2]);
  nor nor_1 (RegWrite, MemWrite, decoder_1_out24[3]);
  or or_1 (ImmSrc[1], decoder_1_out24[3], decoder_1_out27);
  or or_2 (ImmSrc[0], MemWrite, decoder_1_out27);
  nor nor_2 (ALUSrc, decoder_1_out12, decoder_1_out24[3]);
  or or_3 (ResultSrc[1], PCSrc[1], decoder_1_out27, decoder_1_out13);
  or or_4 (ResultSrc[0], decoder_1_out0, decoder_1_out13);
  and and_2 (and_2_out, decoder_1_out24[3], Z, not_4_out, not_3_out);
  or or_5 (PCSrc[0], decoder_1_out27, and_2_out, and_3_out, and_4_out, and_5_out);
  and and_3 (and_3_out, decoder_1_out24[3], not_2_out, not_4_out, F3[0]);
  and and_4 (and_4_out, decoder_1_out24[3], S, F3[2], not_3_out);
  and and_5 (and_5_out, decoder_1_out24[3], not_1_out, F3[2], F3[0]);
  or or_6 (decoder_1_out24[4], decoder_1_out12, decoder_1_out4);
  Decoder #(.select(5)) decoder_2 (
    .out8(decoder_2_out8), .out9(decoder_2_out9), .out12(decoder_2_out12), .out13(decoder_2_out13),
    .out16(decoder_2_out16), .out17(decoder_2_out17), .out18(decoder_2_out18), .out20(decoder_2_out20),
    .out21(decoder_2_out21), .out22(decoder_2_out22), .out23(decoder_2_out23), .sel({decoder_1_out24, F3}),
    .en(and_1_out));  // open: out0, out1, out2, out3, out4, out5, out6, out7, out10, out11, out14, out15, out19, out24, out25, out26, out27, out28, out29, out30, out31
  or or_7 (ALUCtrl[2], decoder_2_out18, decoder_2_out20, decoder_2_out17, decoder_2_out21);
  or or_8 (ALUCtrl[1], decoder_2_out22, decoder_2_out23, decoder_2_out17, decoder_2_out21);
  and and_6 (and_6_out, decoder_2_out16, F7[5], opcode[5]);
  or or_9 (ALUCtrl[0], decoder_2_out8, decoder_2_out9, decoder_2_out12, decoder_2_out13, and_6_out, decoder_2_out18, decoder_2_out22, decoder_2_out21);
endmodule

module Z (
  input  [31:0] I32,
  output ZF
);

  nor nor_1 (ZF, I32[0], I32[1], I32[2], I32[3], I32[4], I32[5], I32[6], I32[7], I32[8], I32[9], I32[10], I32[11], I32[12], I32[13], I32[14], I32[15], I32[17], I32[18], I32[19], I32[20], I32[21], I32[22], I32[23], I32[24], I32[25], I32[26], I32[27], I32[28], I32[29], I32[30], I32[31], I32[16]);
endmodule

module S (
  input  [31:0] I32,
  output SF,
  output [31:0] F
);


  assign F = {{31{1'b0}}, I32[31]};
  assign SF = I32[31];
endmodule

module RegFile (
  input  WE,
  input  [4:0] Addr3,
  input  clk,
  input  [31:0] WD,
  input  [4:0] Addr2,
  input  [4:0] Addr1,
  output [31:0] RD1,
  output [31:0] RD2
);

  wire decoder_1_out1, decoder_1_out2, decoder_1_out3, decoder_1_out4, decoder_1_out5, decoder_1_out6,
       decoder_1_out7, decoder_1_out8, decoder_1_out9, decoder_1_out10, decoder_1_out11, decoder_1_out12,
       decoder_1_out13, decoder_1_out14, decoder_1_out15, decoder_1_out16, decoder_1_out17, decoder_1_out18,
       decoder_1_out19, decoder_1_out20, decoder_1_out21, decoder_1_out22, decoder_1_out23, decoder_1_out24,
       decoder_1_out25, decoder_1_out26, decoder_1_out27, decoder_1_out28, decoder_1_out29, decoder_1_out30,
       decoder_1_out31;
  wire [31:0] a0_q, a1_q, a2_q, a3_q, a4_q, a5_q, a6_q, a7_q, gp_q, ra_q, s0_q, s1_q, s2_q, s3_q, s4_q, s5_q,
       s6_q, s7_q, s8_q, s9_q, s10_q, s11_q, sp_q, t0_q, t1_q, t2_q, t3_q, t4_q, t5_q, t6_q, tp_q;

  Decoder #(.select(5)) decoder_1 (
    .out1(decoder_1_out1), .out2(decoder_1_out2), .out3(decoder_1_out3), .out4(decoder_1_out4),
    .out5(decoder_1_out5), .out6(decoder_1_out6), .out7(decoder_1_out7), .out8(decoder_1_out8),
    .out9(decoder_1_out9), .out10(decoder_1_out10), .out11(decoder_1_out11), .out12(decoder_1_out12),
    .out13(decoder_1_out13), .out14(decoder_1_out14), .out15(decoder_1_out15), .out16(decoder_1_out16),
    .out17(decoder_1_out17), .out18(decoder_1_out18), .out19(decoder_1_out19), .out20(decoder_1_out20),
    .out21(decoder_1_out21), .out22(decoder_1_out22), .out23(decoder_1_out23), .out24(decoder_1_out24),
    .out25(decoder_1_out25), .out26(decoder_1_out26), .out27(decoder_1_out27), .out28(decoder_1_out28),
    .out29(decoder_1_out29), .out30(decoder_1_out30), .out31(decoder_1_out31), .sel(Addr3), .en(WE));  // open: out0
  Register #(.width(32)) s0 (.D(WD), .en(decoder_1_out8), .clk(clk), .Q(s0_q));  // open: clr
  Register #(.width(32)) a6 (.D(WD), .en(decoder_1_out16), .clk(clk), .Q(a6_q));  // open: clr
  Register #(.width(32)) s8 (.D(WD), .en(decoder_1_out24), .clk(clk), .Q(s8_q));  // open: clr
  Register #(.width(32)) ra (.D(WD), .en(decoder_1_out1), .clk(clk), .Q(ra_q));  // open: clr
  Register #(.width(32)) s1 (.D(WD), .en(decoder_1_out9), .clk(clk), .Q(s1_q));  // open: clr
  Register #(.width(32)) a7 (.D(WD), .en(decoder_1_out17), .clk(clk), .Q(a7_q));  // open: clr
  Register #(.width(32)) s9 (.D(WD), .en(decoder_1_out25), .clk(clk), .Q(s9_q));  // open: clr
  Register #(.width(32)) sp (.D(WD), .en(decoder_1_out2), .clk(clk), .Q(sp_q));  // open: clr
  Register #(.width(32)) a0 (.D(WD), .en(decoder_1_out10), .clk(clk), .Q(a0_q));  // open: clr
  Register #(.width(32)) s2 (.D(WD), .en(decoder_1_out18), .clk(clk), .Q(s2_q));  // open: clr
  Register #(.width(32)) s10 (.D(WD), .en(decoder_1_out26), .clk(clk), .Q(s10_q));  // open: clr
  Register #(.width(32)) gp (.D(WD), .en(decoder_1_out3), .clk(clk), .Q(gp_q));  // open: clr
  Register #(.width(32)) a1 (.D(WD), .en(decoder_1_out11), .clk(clk), .Q(a1_q));  // open: clr
  Register #(.width(32)) s3 (.D(WD), .en(decoder_1_out19), .clk(clk), .Q(s3_q));  // open: clr
  Register #(.width(32)) s11 (.D(WD), .en(decoder_1_out27), .clk(clk), .Q(s11_q));  // open: clr
  Register #(.width(32)) tp (.D(WD), .en(decoder_1_out4), .clk(clk), .Q(tp_q));  // open: clr
  Register #(.width(32)) a2 (.D(WD), .en(decoder_1_out12), .clk(clk), .Q(a2_q));  // open: clr
  Register #(.width(32)) s4 (.D(WD), .en(decoder_1_out20), .clk(clk), .Q(s4_q));  // open: clr
  Register #(.width(32)) t3 (.D(WD), .en(decoder_1_out28), .clk(clk), .Q(t3_q));  // open: clr
  Register #(.width(32)) t0 (.D(WD), .en(decoder_1_out5), .clk(clk), .Q(t0_q));  // open: clr
  Register #(.width(32)) a3 (.D(WD), .en(decoder_1_out13), .clk(clk), .Q(a3_q));  // open: clr
  Register #(.width(32)) s5 (.D(WD), .en(decoder_1_out21), .clk(clk), .Q(s5_q));  // open: clr
  Register #(.width(32)) t4 (.D(WD), .en(decoder_1_out29), .clk(clk), .Q(t4_q));  // open: clr
  Register #(.width(32)) t1 (.D(WD), .en(decoder_1_out6), .clk(clk), .Q(t1_q));  // open: clr
  Register #(.width(32)) a4 (.D(WD), .en(decoder_1_out14), .clk(clk), .Q(a4_q));  // open: clr
  Register #(.width(32)) s6 (.D(WD), .en(decoder_1_out22), .clk(clk), .Q(s6_q));  // open: clr
  Register #(.width(32)) t5 (.D(WD), .en(decoder_1_out30), .clk(clk), .Q(t5_q));  // open: clr
  Register #(.width(32)) t2 (.D(WD), .en(decoder_1_out7), .clk(clk), .Q(t2_q));  // open: clr
  Register #(.width(32)) a5 (.D(WD), .en(decoder_1_out15), .clk(clk), .Q(a5_q));  // open: clr
  Register #(.width(32)) s7 (.D(WD), .en(decoder_1_out23), .clk(clk), .Q(s7_q));  // open: clr
  Register #(.width(32)) t6 (.D(WD), .en(decoder_1_out31), .clk(clk), .Q(t6_q));  // open: clr
  Multiplexer #(.enable("false"), .select(5), .width(32)) multiplexer_1 (
    .in0({32{1'b0}}), .in1(ra_q), .in2(sp_q), .in3(gp_q), .in4(tp_q), .in5(t0_q), .in6(t1_q), .in7(t2_q),
    .in8(s0_q), .in9(s1_q), .in10(a0_q), .in11(a1_q), .in12(a2_q), .in13(a3_q), .in14(a4_q), .in15(a5_q),
    .in16(a6_q), .in17(a7_q), .in18(s2_q), .in19(s3_q), .in20(s4_q), .in21(s5_q), .in22(s6_q), .in23(s7_q),
    .in24(s8_q), .in25(s9_q), .in26(s10_q), .in27(s11_q), .in28(t3_q), .in29(t4_q), .in30(t5_q), .in31(t6_q),
    .out(RD1), .sel(Addr1));
  Multiplexer #(.enable("false"), .select(5), .width(32)) multiplexer_2 (
    .in0({32{1'b0}}), .in1(ra_q), .in2(sp_q), .in3(gp_q), .in4(tp_q), .in5(t0_q), .in6(t1_q), .in7(t2_q),
    .in8(s0_q), .in9(s1_q), .in10(a0_q), .in11(a1_q), .in12(a2_q), .in13(a3_q), .in14(a4_q), .in15(a5_q),
    .in16(a6_q), .in17(a7_q), .in18(s2_q), .in19(s3_q), .in20(s4_q), .in21(s5_q), .in22(s6_q), .in23(s7_q),
    .in24(s8_q), .in25(s9_q), .in26(s10_q), .in27(s11_q), .in28(t3_q), .in29(t4_q), .in30(t5_q), .in31(t6_q),
    .out(RD2), .sel(Addr2));
endmodule

module InstrDec (
  input  [31:0] Instr,
  output [6:0] op,
  output [24:0] Imm,
  output [4:0] A3,
  output [19:0] ImmU,
  output [2:0] f3,
  output [4:0] A1,
  output [4:0] A2,
  output [6:0] f7
);


  assign A1 = Instr[19:15];
  assign A2 = Instr[24:20];
  assign A3 = Instr[11:7];
  assign f3 = Instr[14:12];
  assign f7 = Instr[31:25];
  assign Imm = Instr[31:7];
  assign ImmU = Instr[31:12];
  assign op = Instr[6:0];
endmodule

module SignExt (
  input  [24:0] Imm,
  input  [1:0] ImmSrc,
  output [31:0] Imm32
);

  wire [31:0] bit_extender_1_out, bit_extender_2_out, bit_extender_3_out, bit_extender_4_out;

  assign bit_extender_1_out = {{20{Imm[24]}}, Imm[24:13]};  // Bit_Extender bit_extender_1
  assign bit_extender_2_out = {{20{Imm[24]}}, {Imm[24:18], Imm[4:0]}};  // Bit_Extender bit_extender_2
  assign bit_extender_3_out = {{19{Imm[24]}}, {Imm[24], Imm[0], Imm[23:18], Imm[4:1], 1'b0}};  // Bit_Extender bit_extender_3
  assign bit_extender_4_out = {{11{Imm[24]}}, {Imm[24], Imm[12:5], Imm[13], Imm[23:14], 1'b0}};  // Bit_Extender bit_extender_4
  Multiplexer #(.enable("false"), .select(2), .width(32)) multiplexer_1 (
    .in0(bit_extender_1_out), .in1(bit_extender_2_out), .in2(bit_extender_3_out), .in3(bit_extender_4_out),
    .out(Imm32), .sel(ImmSrc));
endmodule

module GGCD (
  input  [31:0] A,
  output [31:0] Instr
);

  ROM #(.addrWidth(7), .dataWidth(32)) rom_1 (.addr(A[8:2]), .data(Instr));

  // Notes on the sheet:
  //   contents of rom_1 (hex, n*v repeats v):
  //   2137 ffc10113 40000193 fd010113 2112823 2812623 3010413 1a000213 fc442e23 3400213 fe442023 d000213
  //   fe442223 1a00213 fe442423 d00213 fe442623 34000213 fe442823 600593 fdc40513 f4000ef fca42c23
  //   fd842203 513 3012083 2c12403 3010113 6f fd010113 2112823 2812623 3010413 213 fe442623 213 fe442823
  //   4058463 b55663 fea42823 3c0006f fea42023 fcb42e23 fdc42583 fdc42203 fe042283 40428533 fb9ff0ef
  //   fea42623 feb42823 fdc42583 fe042503 fec42203 120213 fe442623 fec42503 ff042583 3012083 2c12403
  //   3010113 8067 fd010113 2112823 2812623 3010413 2058863 feb42823 fea42023 fcb42e23 fdc42583 fe042503
  //   f59ff0ef fcb42e23 fdc42583 fe042503 ff042503 fd5ff06f 50513 3012083 2c12403 3010113 8067 fd010113
  //   2112823 2812623 3010413 52203 fe442823 100213 fe442623 fec42203 4b25263 feb42023 fca42e23 fec42203
  //   221213 fdc42503 450233 22583 ff042503 f65ff0ef fea42823 fe042583 fdc42503 fec42203 120213 fe442623
  //   fbdff06f ff042503 3012083 2c12403 3010113 8067
endmodule

module sll12 (
  input  [19:0] UImm,
  output [31:0] UImm32
);


  assign UImm32 = {UImm, {12{1'b0}}};
endmodule
